// Logisim project computer.circ as structural Verilog: 1 circuit, main circuit main
module main (
  input  in_1,
  input  in_2
);

  wire adder_1_cout, and_1_out, and_3_out, and_5_out, and_6_out, and_7_out, and_8_out, and_9_out, and_10_out,
       and_11_out, and_12_out, and_13_out, and_14_out, and_16_out, and_17_out, and_18_out, and_19_out,
       and_20_out, and_21_out, and_22_out, and_23_out, and_24_out, and_25_out, and_26_out, and_27_out,
       and_28_out, and_29_out, and_30_out, and_31_out, and_32_out, and_34_out, and_35_out, and_38_out,
       and_39_out, and_40_out, and_41_out, and_42_out, and_44_out, and_46_out, and_47_out, and_48_out,
       and_49_out, and_50_out, and_51_out, and_52_out, and_53_out, and_54_out, and_55_out, and_56_out,
       and_57_out, and_58_out, and_59_out, and_60_out, and_61_out, and_62_out, and_64_out, and_65_out,
       and_66_out, and_67_out, and_68_out, and_69_out, and_70_out, and_71_out, and_72_out, and_73_out,
       and_74_out, and_75_out, and_76_out, and_77_out, and_78_out, and_79_out, and_80_out, and_81_out,
       and_82_out, and_83_out, and_84_out, and_85_out, and_86_out, and_87_out, and_88_out, and_89_out,
       and_90_out, and_91_out, bit_extender_4_out, clock_1_out, comparator_2_lt, comparator_3_gt,
       comparator_4_eq, comparator_5_eq, comparator_6_lt, comparator_7_gt, comparator_8_eq, comparator_9_eq,
       comparator_10_eq, comparator_11_eq, comparator_11_lt, comparator_12_eq, comparator_13_eq, d_ff_1_q,
       d_ff_2_q, d_ff_3_q, d_ff_4_q, d_ff_5_q, d_ff_6_q, d_ff_7_q, d_ff_8_q, decoder_1_out0, decoder_1_out1,
       decoder_2_out0, decoder_2_out1, decoder_2_out2, decoder_2_out3, decoder_2_out4, decoder_2_out5,
       decoder_2_out6, decoder_2_out7, decoder_3_out1, decoder_4_out0, decoder_4_out1, decoder_4_out2,
       decoder_4_out3, decoder_4_out4, decoder_4_out5, decoder_4_out6, decoder_4_out7, decoder_4_out8,
       decoder_4_out9, decoder_4_out10, decoder_4_out11, decoder_4_out12, decoder_4_out13, decoder_4_out14,
       decoder_4_out15, decoder_5_out0, decoder_5_out1, decoder_5_out2, decoder_5_out3, decoder_5_out4,
       decoder_5_out5, decoder_5_out6, decoder_6_out2, decoder_6_out3, ENTER_q, INSTR_MODE_q,
       jmp_correction_q, KERNEL_MODE_q, keyboard_1_avail, multiplexer_2_out, nor_2_out, not_1_out, not_2_out,
       not_3_out, not_4_out, not_5_out, not_6_out, not_7_out, not_8_out, not_9_out, not_10_out, not_11_out,
       not_12_out, not_13_out, not_14_out, not_15_out, not_16_out, not_17_out, not_18_out, not_19_out,
       not_20_out, not_21_out, not_22_out, not_23_out, not_24_out, not_25_out, not_26_out, not_27_out,
       not_28_out, not_29_out, not_30_out, not_31_out, not_32_out, not_33_out, not_34_out, not_35_out,
       not_36_out, not_37_out, not_38_out, not_39_out, not_40_out, not_41_out, not_42_out, not_43_out,
       not_44_out, not_45_out, not_46_out, not_47_out, not_48_out, not_49_out, not_50_out, not_51_out,
       not_52_out, not_53_out, not_54_out, not_55_out, not_56_out, not_57_out, not_58_out, not_59_out,
       not_60_out, not_61_out, not_62_out, not_63_out, not_64_out, not_65_out, not_66_out, not_67_out,
       not_68_out, not_69_out, not_70_out, not_71_out, not_72_out, not_73_out, not_74_out, not_75_out,
       not_76_out, not_77_out, not_78_out, not_79_out, not_80_out, not_81_out, not_82_out, not_83_out,
       not_84_out, not_85_out, not_86_out, not_87_out, not_88_out, or_1_out, or_2_out, or_3_out, or_4_out,
       or_5_out, or_6_out, or_7_out, or_8_out, or_10_out, or_11_out, or_12_out, or_13_out, or_14_out,
       or_16_out, or_17_out, or_18_out, or_21_out, or_22_out, or_23_out, or_25_out, or_26_out, or_27_out,
       or_28_out, or_29_out, or_31_out, or_32_out, or_33_out, or_34_out, or_35_out, or_36_out, or_37_out,
       or_39_out, or_40_out, or_41_out, or_42_out, or_43_out, or_45_out, or_46_out, or_47_out, or_48_out,
       or_49_out, or_50_out, or_51_out, or_52_out, or_53_out, or_55_out, or_57_out, or_58_out, or_59_out,
       or_61_out, PHASE_q, pla_1_out, priority_encoder_1_p2, priority_encoder_1_p3, priority_encoder_1_p4,
       priority_encoder_1_p5, priority_encoder_2_p3, priority_encoder_2_p4, priority_encoder_2_p5,
       priority_encoder_2_p6, priority_encoder_2_p7, priority_encoder_2_p8, priority_encoder_2_p9,
       priority_encoder_3_p2, priority_encoder_3_p5, priority_encoder_3_p6, priority_encoder_5_p1,
       priority_encoder_5_p4, subtractor_1_bout, xor_1_out, xor_2_out, xor_3_out, xor_4_out, xor_6_out,
       xor_7_out, xor_8_out, xor_9_out, xor_10_out;
  wire [0:0] demultiplexer_1_out4;
  wire [1:0] and_63_out, demultiplexer_1_out2, KBD_PLA_out, multiplexer_27_out_2, multiplexer_31_out, PC_q_2,
       priority_encoder_1_p1, priority_encoder_3_p3, priority_encoder_4_out, priority_encoder_5_p2,
       TERM_PLA_out, TWO_TMP_q;
  wire [2:0] ADC_SBC_SELECT_q, ADC_SBC_SELECT_q_2, demultiplexer_1_out1, demultiplexer_1_out4_2, IR_q_2,
       IR_q_3, multiplexer_4_out, multiplexer_32_out, priority_encoder_2_p1, SHIFT_AMT_q;
  wire [3:0] adder_3_out, and_4_out, COPY_MODE_q, demultiplexer_1_out0, demultiplexer_1_out0_2,
       demultiplexer_1_out4_3, FLAGS_q, multiplexer_1_out, register_1_q, register_1_q_2, register_1_q_3,
       register_1_q_4, register_1_q_5, register_1_q_6, register_2_q, TOTAL_SYSCALLS_q_2, TOTAL_SYSCALLS_q_3,
       TOTAL_SYSCALLS_q_4;
  wire [4:0] demultiplexer_1_out1_2;
  wire [4:3] IR_q_4;
  wire [6:0] keyboard_1_data, multiplexer_11_out;
  wire [6:6] multiplexer_11_out_2;
  wire [7:0] adder_1_out, adder_7_out, and_15_out, bit_extender_2_out, bit_extender_3_out,
       bit_extender_5_out, bit_extender_6_out, bit_extender_7_out, demultiplexer_1_out3,
       demultiplexer_1_out5, demultiplexer_1_out6, ERR_INFO_q, INT_TIMER_q, IR_q_5, LDI_DATA_q,
       Main_RAM_dout, multiplexer_5_out, multiplexer_6_out, multiplexer_7_out, multiplexer_8_out,
       multiplexer_9_out, multiplexer_21_out, multiplexer_25_out, multiplexer_27_out, multiplexer_33_out,
       multiplexer_34_out, multiplexer_35_out, or_9_out, PC_HI_2_RET_q, PC_LO_8_q, PC_LO_8_RET_q, PC_q, R0_q,
       R1_q, R2_q, R3_q, R4_q, R5_q, R6_q, R7_q, shifter_1_out, shifter_2_out, subtractor_1_out, TST_LED_q,
       xor_5_out;
  wire [7:2] demultiplexer_1_out2_2;
  wire [9:0] adder_5_out, adder_6_out, adder_8_out, adder_9_out, CALL_RET_ADDR_q, CALL_STACK_POINTER_q,
       INT_RET_ADDR_q, multiplexer_3_out, multiplexer_10_out, multiplexer_12_out, multiplexer_13_out,
       multiplexer_14_out, multiplexer_15_out, multiplexer_16_out, multiplexer_17_out, multiplexer_18_out,
       multiplexer_19_out, multiplexer_20_out, multiplexer_26_out, multiplexer_28_out, multiplexer_29_out,
       multiplexer_30_out, PGRM_START_ADDR_q, STACK_POINTER_q, subtractor_2_out, subtractor_3_out,
       subtractor_4_out, SYSRET_ADDR_q;
  wire [9:8] bit_extender_1_out;
  wire [11:0] TOTAL_SYSCALLS_q;
  wire [18:8] IR_q;
  wire [23:0] adder_2_out, adder_10_out, IRAM_dout, multiplexer_22_out, multiplexer_23_out,
       multiplexer_24_out, ROM0_BOOT_data, ROM1_TERMINAL_data;
  wire [31:0] adder_4_out, TOTAL_CYCLES_q;

  Register #(.width(3)) SHIFT_AMT (
    .D(demultiplexer_1_out1), .en(decoder_5_out1), .clk(clock_1_out), .Q(SHIFT_AMT_q));  // open: clr
  Register #(.trigger("high"), .width(6)) ADC_SBC_SELECT (
    .D(6'b001000), .en(1'b1), .clk(1'b1), .Q({ADC_SBC_SELECT_q_2, ADC_SBC_SELECT_q}));  // open: clr
  and and_1 (and_1_out, and_48_out, decoder_5_out0);
  xor xor_1 (xor_1_out, multiplexer_9_out[7], decoder_1_out1);
  xor xor_2 (xor_2_out, multiplexer_6_out[7], xor_1_out);
  not not_1 (not_1_out, xor_2_out);
  and and_2 (and_4_out[3], not_1_out, xor_3_out);
  Comparator comparator_1 (
    .a({multiplexer_11_out_2[6], multiplexer_11_out}), .b({8{1'b0}}), .eq(and_4_out[1]), .lt(and_4_out[2]));  // open: gt
  or or_1 (or_1_out, priority_encoder_1_p2, or_27_out);
  Multiplexer #(.width(4)) multiplexer_1 (
    .in0(and_4_out), .in1(demultiplexer_1_out0), .out(multiplexer_1_out), .sel(and_1_out));
  Register #(.width(24)) register_1 (
    .D(adder_2_out), .en(and_3_out), .clk(clock_1_out),
    .Q({register_1_q_6, register_1_q_5, register_1_q_4, register_1_q_3, register_1_q_2, register_1_q}));  // open: clr
  and and_3 (and_3_out, and_51_out, and_16_out);
  or or_2 (or_2_out, and_56_out, and_51_out);
  xor xor_3 (xor_3_out, multiplexer_6_out[7], multiplexer_11_out_2[6]);
  Decoder #(.select(3)) decoder_1 (
    .out0(decoder_1_out0), .out1(decoder_1_out1), .sel(multiplexer_4_out), .en(or_8_out));  // open: out2, out3, out4, out5, out6, out7
  or or_3 (or_3_out, decoder_1_out0, or_27_out, decoder_1_out1);
  Multiplexer multiplexer_2 (.in0(adder_1_cout), .in1(not_2_out), .out(multiplexer_2_out), .sel(decoder_1_out1));
  and and_4 (and_4_out[0], or_3_out, multiplexer_2_out);
  Register #(.width(4)) FLAGS (.D(multiplexer_1_out), .en(or_4_out), .clk(clock_1_out), .Q(FLAGS_q));  // open: clr
  or or_4 (or_4_out, or_1_out, and_1_out, nor_2_out);
  Clock clock_1 (.out(clock_1_out));
  Register R4 (
    .D({multiplexer_11_out_2[6], multiplexer_11_out}), .en(decoder_2_out4), .clk(clock_1_out), .Q(R4_q));  // open: clr
  D_Flip_Flop d_ff_1 (.D(xor_4_out), .clk(clock_1_out), .Q(d_ff_1_q));  // open: Qn, preset, reset
  xor xor_4 (xor_4_out, d_ff_4_q, or_2_out);
  Register PC_LO_8_RET (.D(multiplexer_33_out), .en(and_5_out), .clk(clock_1_out), .Q(PC_LO_8_RET_q), .clr(d_ff_4_q));
  and and_5 (and_5_out, and_16_out, and_56_out);
  and and_6 (and_6_out, FLAGS_q[0], not_5_out);
  Adder adder_1 (.a(multiplexer_9_out), .b(multiplexer_6_out), .out(adder_1_out), .cin(and_6_out), .cout(adder_1_cout));
  not not_2 (not_2_out, subtractor_1_bout);
  LED led_1 (.in(FLAGS_q[2]));
  LED led_2 (.in(FLAGS_q[1]));
  LED led_3 (.in(FLAGS_q[0]));
  LED led_4 (.in(FLAGS_q[3]));
  not not_3 (not_3_out, d_ff_1_q);
  Adder #(.width(24)) adder_2 (
    .a({register_1_q_6, register_1_q_5, register_1_q_4, register_1_q_3, register_1_q_2, register_1_q}),
    .b(24'h1), .out(adder_2_out));  // open: cin, cout
  and and_7 (and_7_out, and_56_out, d_ff_2_q);
  not not_4 (not_4_out, priority_encoder_1_p2);
  not not_5 (not_5_out, priority_encoder_1_p5);
  and and_8 (and_8_out, not_5_out, not_4_out, not_6_out);
  Subtractor subtractor_1 (
    .a(multiplexer_6_out), .b(multiplexer_9_out), .out(subtractor_1_out), .bin(and_8_out),
    .bout(subtractor_1_bout));
  Register R0 (
    .D({multiplexer_11_out_2[6], multiplexer_11_out}), .en(decoder_2_out0), .clk(clock_1_out), .Q(R0_q));  // open: clr
  not not_6 (not_6_out, FLAGS_q[0]);
  Register R1 (
    .D({multiplexer_11_out_2[6], multiplexer_11_out}), .en(decoder_2_out1), .clk(clock_1_out), .Q(R1_q));  // open: clr
  Register R2 (
    .D({multiplexer_11_out_2[6], multiplexer_11_out}), .en(decoder_2_out2), .clk(clock_1_out), .Q(R2_q));  // open: clr
  Register R3 (
    .D({multiplexer_11_out_2[6], multiplexer_11_out}), .en(decoder_2_out3), .clk(clock_1_out), .Q(R3_q));  // open: clr
  Register R5 (
    .D({multiplexer_11_out_2[6], multiplexer_11_out}), .en(decoder_2_out5), .clk(clock_1_out), .Q(R5_q));  // open: clr
  Multiplexer #(.width(10)) multiplexer_3 (
    .in0(multiplexer_30_out), .in1({bit_extender_1_out, PC_LO_8_RET_q}), .out(multiplexer_3_out),
    .sel(and_56_out));
  Register #(.width(4)) register_2 (
    .D(adder_3_out), .en(or_2_out), .clk(clock_1_out), .Q(register_2_q), .clr(d_ff_4_q));
  and and_9 (and_9_out, and_51_out, and_16_out);
  Register PC_HI_2_RET (.D(multiplexer_33_out), .en(and_7_out), .clk(clock_1_out), .Q(PC_HI_2_RET_q), .clr(d_ff_4_q));
  or or_5 (or_5_out, d_ff_2_q, and_16_out, and_17_out);
  and and_10 (and_10_out, or_5_out, and_51_out);
  and and_11 (and_11_out, or_5_out, and_56_out);
  Multiplexer #(.select(2), .width(3)) multiplexer_4 (
    .in0(3'b001), .in1(ADC_SBC_SELECT_q_2), .in2(ADC_SBC_SELECT_q), .in3(IR_q_3), .out(multiplexer_4_out),
    .sel(priority_encoder_1_p1));
  Shifter shifter_1 (.in(multiplexer_6_out), .\dist (SHIFT_AMT_q), .out(shifter_1_out));
  Register #(.width(10)) CALL_RET_ADDR (
    .D(multiplexer_3_out), .en(or_7_out), .clk(clock_1_out), .Q(CALL_RET_ADDR_q));  // open: clr
  Adder #(.width(4)) adder_3 (.a(register_2_q), .b(4'b0001), .out(adder_3_out));  // open: cin, cout
  and and_12 (and_12_out, and_56_out, d_ff_3_q);
  D_Flip_Flop d_ff_2 (.D(and_16_out), .clk(not_8_out), .Q(d_ff_2_q));  // open: Qn, preset, reset
  Bit_Extender #(.out_width(2)) bit_extender_1 (.in(PC_HI_2_RET_q), .out(bit_extender_1_out));
  or or_6 (or_6_out, and_16_out, d_ff_2_q);
  // Priority_Encoder #(.select(2)) priority_encoder_1: pin names not known; wires that end beside it: priority_encoder_1_p1, priority_encoder_1_p2, priority_encoder_1_p3, priority_encoder_1_p4, priority_encoder_1_p5
  Multiplexer #(.enable("true"), .select(3), .width(8)) multiplexer_5 (
    .in0(adder_1_out), .in1(subtractor_1_out), .in2(shifter_1_out), .in3(shifter_2_out), .in4(and_15_out),
    .in5(or_9_out), .in6(xor_5_out), .in7({8{1'b0}}), .out(multiplexer_5_out), .sel(multiplexer_4_out),
    .en(or_8_out));
  Shifter #(.shift("lr")) shifter_2 (.in(multiplexer_6_out), .\dist (SHIFT_AMT_q), .out(shifter_2_out));
  Multiplexer #(.select(3), .width(8)) multiplexer_6 (
    .in0(R0_q), .in1(R1_q), .in2(R2_q), .in3(R3_q), .in4(R4_q), .in5(R5_q), .in6(R6_q), .in7(R7_q),
    .out(multiplexer_6_out), .sel(IR_q[18:16]));
  Register R6 (
    .D({multiplexer_11_out_2[6], multiplexer_11_out}), .en(decoder_2_out6), .clk(clock_1_out), .Q(R6_q));  // open: clr
  Comparator #(.mode("unsigned"), .width(4)) comparator_2 (
    .a(adder_3_out), .b(4'b0011), .lt(comparator_2_lt));  // open: gt, eq
  or or_7 (or_7_out, and_9_out, and_12_out);
  D_Flip_Flop d_ff_3 (.D(d_ff_2_q), .clk(not_8_out), .Q(d_ff_3_q));  // open: Qn, preset, reset
  and and_13 (and_13_out, and_56_out, or_6_out);
  and and_14 (and_14_out, and_51_out, or_6_out);
  assign and_15_out = multiplexer_9_out & multiplexer_6_out;  // AND_Gate and_15, 8 bits wide
  Decoder #(.select(3)) decoder_2 (
    .out0(decoder_2_out0), .out1(decoder_2_out1), .out2(decoder_2_out2), .out3(decoder_2_out3),
    .out4(decoder_2_out4), .out5(decoder_2_out5), .out6(decoder_2_out6), .out7(decoder_2_out7),
    .sel(IR_q[18:16]), .en(and_18_out));
  and and_16 (and_16_out, comparator_2_lt, comparator_3_gt);
  D_Flip_Flop d_ff_4 (.D(d_ff_3_q), .clk(not_8_out), .Q(d_ff_4_q));  // open: Qn, preset, reset
  and and_17 (and_17_out, d_ff_3_q, clock_1_out);
  not not_7 (not_7_out, not_8_out);
  Multiplexer #(.width(8)) multiplexer_7 (
    .in0(bit_extender_2_out), .in1(PC_LO_8_q), .out(multiplexer_7_out), .sel(d_ff_2_q));
  Register LDI_DATA (.D(IR_q_5), .en(priority_encoder_2_p3), .clk(clock_1_out), .Q(LDI_DATA_q));  // open: clr
  or or_8 (or_8_out, or_27_out, priority_encoder_1_p2, priority_encoder_1_p5);
  assign or_9_out = multiplexer_9_out | multiplexer_6_out;  // OR_Gate or_9, 8 bits wide
  Register R7 (
    .D({multiplexer_11_out_2[6], multiplexer_11_out}), .en(decoder_2_out7), .clk(clock_1_out), .Q(R7_q));  // open: clr
  Register PC_LO_8 (.D(PC_q), .en(d_ff_1_q), .clk(clock_1_out), .Q(PC_LO_8_q), .clr(d_ff_4_q));
  assign bit_extender_2_out = {{6{1'b0}}, PC_q_2};  // Bit_Extender bit_extender_2
  Register PC_HI_2 (.D(bit_extender_2_out), .en(d_ff_1_q), .clk(clock_1_out), .clr(d_ff_4_q));  // open: Q
  Comparator #(.mode("unsigned"), .width(4)) comparator_3 (
    .a(adder_3_out), .b(4'b0001), .gt(comparator_3_gt));  // open: eq, lt
  Register #(.width(32)) TOTAL_CYCLES (
    .D(adder_4_out), .en(not_7_out), .clk(clock_1_out), .Q(TOTAL_CYCLES_q));  // open: clr
  assign xor_5_out = multiplexer_9_out ^ multiplexer_6_out;  // XOR_Gate xor_5, 8 bits wide
  or or_10 (or_10_out, or_8_out, and_41_out, or_28_out, priority_encoder_2_p6);
  Multiplexer #(.select(3), .width(8)) multiplexer_8 (
    .in0(R0_q), .in1(R1_q), .in2(R2_q), .in3(R3_q), .in4(R4_q), .in5(R5_q), .in6(R6_q), .in7(R7_q),
    .out(multiplexer_8_out), .sel(multiplexer_32_out));
  Multiplexer #(.select(3), .width(8)) multiplexer_9 (
    .in0(R0_q), .in1(R1_q), .in2(R2_q), .in3(R3_q), .in4(R4_q), .in5(R5_q), .in6(R6_q), .in7(R7_q),
    .out(multiplexer_9_out), .sel(IR_q_2));
  Multiplexer #(.width(10)) multiplexer_10 (
    .in0(CALL_RET_ADDR_q), .in1(PGRM_START_ADDR_q), .out(multiplexer_10_out), .sel(and_19_out));
  not not_8 (not_8_out, not_39_out);
  Adder #(.width(32)) adder_4 (.a(TOTAL_CYCLES_q), .b(32'h1), .out(adder_4_out));  // open: cin, cout
  Multiplexer #(.select(3), .width(8)) multiplexer_11 (
    .in0(multiplexer_5_out), .in1(LDI_DATA_q), .in2(multiplexer_9_out), .in3(multiplexer_6_out),
    .in4(multiplexer_21_out), .in5(multiplexer_33_out), .in6(multiplexer_27_out),
    .out({multiplexer_11_out_2[6], multiplexer_11_out}), .sel(priority_encoder_2_p1));  // open: in7
  nor nor_1 (priority_encoder_1_p5, IR_q_4[3], IR_q_4[4]);
  not not_9 (not_9_out, priority_encoder_1_p2);
  not not_10 (not_10_out, and_22_out);
  and and_18 (and_18_out, not_9_out, or_10_out, not_29_out, not_10_out, not_39_out);
  or or_11 (or_11_out, and_19_out, d_ff_4_q);
  and and_19 (and_19_out, d_ff_5_q, not_22_out);
  nor nor_2 (nor_2_out, IR_q_4[4], IR_q_4[3]);
  not not_11 (not_11_out, IR_q_4[4]);
  not not_12 (not_12_out, IR_q_3[2]);
  not not_13 (not_13_out, IR_q_3[1]);
  not not_14 (not_14_out, not_11_out);
  and and_20 (and_20_out, IR_q_4[3], not_12_out, not_11_out, not_13_out, not_24_out);
  not not_15 (not_15_out, IR_q_4[3]);
  not not_16 (not_16_out, IR_q_3[2]);
  not not_17 (not_17_out, IR_q_3[1]);
  and and_21 (and_21_out, not_14_out, not_15_out, not_16_out, not_17_out, not_26_out);
  and and_22 (and_22_out, and_21_out, not_18_out);
  not not_18 (not_18_out, in_1);
  not not_19 (not_19_out, and_22_out);
  not not_20 (not_20_out, not_39_out);
  D_Flip_Flop jmp_correction (.D(or_12_out), .clk(clock_1_out), .Q(jmp_correction_q));  // open: Qn, preset, reset
  or or_12 (or_12_out, priority_encoder_3_p2, and_63_out[1], or_11_out, priority_encoder_3_p5);
  not not_21 (not_21_out, or_40_out);
  and and_23 (and_23_out, not_39_out, or_13_out);
  and and_24 (and_24_out, not_39_out, or_40_out);
  or or_13 (or_13_out, and_13_out, and_14_out);
  Comparator #(.mode("unsigned"), .width(3)) comparator_4 (
    .a(COPY_MODE_q[3:1]), .b(3'b000), .eq(comparator_4_eq));  // open: gt, lt
  ROM #(.addrWidth(10), .dataWidth(24)) ROM1_TERMINAL (.addr({PC_q_2, PC_q}), .data(ROM1_TERMINAL_data));
  not not_22 (not_22_out, comparator_4_eq);
  Comparator #(.width(3)) comparator_5 (.a(IR_q_3), .b(3'b111), .eq(comparator_5_eq));  // open: gt, lt
  not not_23 (not_23_out, IR_q_4[3]);
  not not_24 (not_24_out, IR_q_3[0]);
  not not_25 (not_25_out, IR_q_3[1]);
  and and_25 (and_25_out, and_21_out, not_27_out);
  not not_26 (not_26_out, IR_q_3[0]);
  not not_27 (not_27_out, and_22_out);
  not not_28 (not_28_out, or_21_out);
  Register #(.width(10)) CALL_STACK_POINTER (
    .D(multiplexer_12_out), .en(or_14_out), .clk(clock_1_out), .Q(CALL_STACK_POINTER_q));  // open: clr
  or or_14 (or_14_out, and_23_out, and_57_out);
  Multiplexer #(.width(10)) multiplexer_12 (
    .in0(multiplexer_16_out), .in1(subtractor_3_out), .out(multiplexer_12_out), .sel(and_57_out));
  and and_26 (and_26_out, comparator_5_eq, KERNEL_MODE_q, and_27_out);
  and and_27 (and_27_out, not_11_out, not_23_out);
  not not_29 (not_29_out, and_26_out);
  and and_28 (and_28_out, or_17_out, not_34_out);
  // Priority_Encoder priority_encoder_2: pin names not known; wires that end beside it: priority_encoder_2_p1, and_28_out, priority_encoder_2_p3, priority_encoder_2_p4, priority_encoder_2_p5, priority_encoder_2_p6, priority_encoder_2_p7, priority_encoder_2_p8, priority_encoder_2_p9
  not not_30 (not_30_out, IR_q_3[2]);
  or or_15 (priority_encoder_2_p3, and_61_out, and_29_out);
  and and_29 (and_29_out, IR_q_4[3], not_25_out, not_11_out, not_30_out, IR_q_3[0]);
  not not_31 (not_31_out, IR_q_4[3]);
  not not_32 (not_32_out, IR_q_3[2]);
  not not_33 (not_33_out, IR_q_3[1]);
  and and_30 (and_30_out, not_14_out, not_31_out, not_32_out, not_33_out, IR_q_3[0]);
  Comparator #(.mode("unsigned"), .width(10)) comparator_6 (
    .a(multiplexer_20_out), .b(10'h112), .lt(comparator_6_lt));  // open: gt, eq
  Multiplexer #(.width(10)) multiplexer_13 (
    .in0(multiplexer_18_out), .in1(10'h6), .out(multiplexer_13_out), .sel(and_63_out[0]));
  Comparator #(.mode("unsigned"), .width(10)) comparator_7 (
    .a(multiplexer_20_out), .b({10{1'b0}}), .gt(comparator_7_gt));  // open: eq, lt
  Multiplexer #(.width(10)) multiplexer_14 (
    .in0(multiplexer_13_out), .in1(10'h30), .out(multiplexer_14_out), .sel(comparator_8_eq));
  Multiplexer #(.select(2), .width(10)) multiplexer_15 (
    .in0(adder_5_out), .in1(multiplexer_19_out), .in2(multiplexer_10_out), .in3(multiplexer_14_out),
    .out(multiplexer_15_out), .sel(priority_encoder_3_p3));
  Register #(.width(10)) PC (.D(multiplexer_15_out), .en(or_16_out), .clk(clock_1_out), .Q({PC_q_2, PC_q}), .clr(in_1));
  or or_16 (or_16_out, priority_encoder_3_p5, and_38_out, jmp_correction_q, priority_encoder_3_p2, or_11_out, and_63_out[1]);
  Register #(.width(1)) PHASE (.D(not_39_out), .en(1'b1), .clk(clock_1_out), .Q(PHASE_q));  // open: clr
  Multiplexer #(.select(2), .width(10)) multiplexer_16 (
    .in0(adder_8_out), .in1(subtractor_2_out), .in2(STACK_POINTER_q), .in3(multiplexer_29_out),
    .out(multiplexer_16_out), .sel(priority_encoder_4_out));
  not not_34 (not_34_out, and_26_out);
  or or_17 (or_17_out, priority_encoder_1_p2, or_27_out, or_18_out, priority_encoder_1_p5);
  or or_18 (or_18_out, priority_encoder_2_p9, or_36_out);
  or or_19 (priority_encoder_2_p5, or_21_out, and_53_out);
  not not_35 (not_35_out, IR_q_3[2]);
  not not_36 (not_36_out, IR_q_3[0]);
  or or_20 (priority_encoder_2_p9, and_22_out, and_25_out, and_31_out);
  and and_31 (and_31_out, IR_q_4[3], not_35_out, not_11_out, IR_q_3[1], not_36_out);
  not not_37 (not_37_out, IR_q_4[3]);
  or or_21 (or_21_out, and_30_out, and_34_out);
  not not_38 (not_38_out, KERNEL_MODE_q);
  and and_32 (and_32_out, comparator_6_lt, not_38_out, comparator_7_gt);
  or or_22 (or_22_out, not_28_out, not_43_out);
  // Priority_Encoder #(.select(2)) priority_encoder_3: pin names not known; wires that end beside it: or_22_out, priority_encoder_3_p2, priority_encoder_3_p3, or_11_out, priority_encoder_3_p5, priority_encoder_3_p6
  not not_39 (not_39_out, PHASE_q);
  Multiplexer #(.width(10)) multiplexer_17 (
    .in0(STACK_POINTER_q), .in1(CALL_STACK_POINTER_q), .out(multiplexer_17_out), .sel(not_21_out));
  Register #(.width(10)) STACK_POINTER (
    .D(multiplexer_16_out), .en(or_23_out), .clk(clock_1_out), .Q(STACK_POINTER_q));  // open: clr
  or or_23 (or_23_out, and_57_out, and_24_out);
  or or_24 (priority_encoder_2_p4, and_62_out, or_25_out);
  or or_25 (or_25_out, and_48_out, and_47_out, and_20_out);
  not not_40 (not_40_out, IR_q_3[2]);
  and and_33 (priority_encoder_2_p8, IR_q_4[3], not_40_out, not_11_out, IR_q_3[1], IR_q_3[0]);
  not not_41 (not_41_out, IR_q_3[2]);
  not not_42 (not_42_out, IR_q_3[0]);
  and and_34 (and_34_out, not_14_out, not_37_out, not_41_out, IR_q_3[1], not_42_out);
  Multiplexer #(.width(10)) multiplexer_18 (
    .in0(SYSRET_ADDR_q), .in1(INT_RET_ADDR_q), .out(multiplexer_18_out), .sel(and_26_out));
  Register #(.width(10)) SYSRET_ADDR (
    .D(adder_6_out), .en(and_35_out), .clk(clock_1_out), .Q(SYSRET_ADDR_q));  // open: clr
  and and_35 (and_35_out, and_63_out[0], not_20_out);
  Multiplexer #(.width(10)) multiplexer_19 (
    .in0(multiplexer_20_out), .in1(10'h102), .out(multiplexer_19_out), .sel(and_32_out));
  Multiplexer #(.width(10)) multiplexer_20 (
    .in0(multiplexer_26_out), .in1(adder_9_out), .out(multiplexer_20_out), .sel(and_34_out));
  not not_43 (not_43_out, priority_encoder_3_p2);
  Adder #(.width(10)) adder_5 (.a({PC_q_2, PC_q}), .b(10'h1), .out(adder_5_out));  // open: cin, cout
  Register INT_TIMER (.D(adder_7_out), .en(1'b0), .clk(clock_1_out), .Q(INT_TIMER_q));  // open: clr
  Priority_Encoder #(.select(2)) priority_encoder_4 (
    .in0(or_26_out), .in1(or_29_out), .in3(and_57_out), .out(priority_encoder_4_out));  // open: in2
  or or_26 (or_26_out, and_65_out, and_13_out);
  Multiplexer #(.enable("true"), .select(3), .width(8)) multiplexer_21 (
    .in0({4'b0000, FLAGS_q}), .in1({{5{1'b0}}, SHIFT_AMT_q}), .in2({{6{1'b0}}, TWO_TMP_q}), .in3(TST_LED_q),
    .in4(bit_extender_3_out), .in5(ERR_INFO_q), .out(multiplexer_21_out), .sel(IR_q_2),
    .en(priority_encoder_2_p6));  // open: in6, in7
  or or_27 (or_27_out, priority_encoder_1_p3, priority_encoder_1_p4);
  not not_44 (not_44_out, IR_q_3[1]);
  and and_36 (priority_encoder_1_p4, IR_q_4[3], IR_q_3[2], not_11_out, not_44_out, not_48_out);
  or or_28 (or_28_out, and_20_out, and_29_out, or_31_out, priority_encoder_2_p8, priority_encoder_1_p4, priority_encoder_1_p3);
  not not_45 (not_45_out, IR_q_4[3]);
  not not_46 (not_46_out, IR_q_3[2]);
  and and_37 (priority_encoder_1_p2, not_14_out, not_45_out, not_46_out, IR_q_3[1], IR_q_3[0]);
  Adder #(.width(10)) adder_6 (.a({PC_q_2, PC_q}), .b({10{1'b0}}), .out(adder_6_out));  // open: cin, cout
  and and_38 (and_38_out, not_39_out, not_19_out, not_3_out);
  ROM #(.addrWidth(10), .dataWidth(24)) ROM0_BOOT (.addr({PC_q_2, PC_q}), .data(ROM0_BOOT_data));
  Adder adder_7 (.a(INT_TIMER_q), .b(8'h1), .out(adder_7_out));  // open: cin, cout
  Adder #(.width(10)) adder_8 (.a(multiplexer_17_out), .b(10'h1), .out(adder_8_out));  // open: cin, cout
  Comparator comparator_8 (.a(adder_7_out), .b({8{1'b1}}), .eq(comparator_8_eq));  // open: gt, lt
  Subtractor #(.width(10)) subtractor_2 (.a(multiplexer_17_out), .b(10'h1), .out(subtractor_2_out));  // open: bin, bout
  Subtractor #(.width(10)) subtractor_3 (
    .a(multiplexer_16_out), .b(10'h40), .out(subtractor_3_out));  // open: bin, bout
  or or_29 (or_29_out, and_62_out, and_14_out);
  RAM #(.addrWidth(10), .asyncread("true"), .dataWidth(24)) IRAM (
    .addr({PC_q_2, PC_q}), .we(and_39_out), .oe(INSTR_MODE_q), .clk(clock_1_out), .din(multiplexer_22_out),
    .dout(IRAM_dout));
  and and_39 (and_39_out, not_51_out, COPY_MODE_q[0]);
  Multiplexer #(.select(3), .width(24)) multiplexer_22 (
    .in0(ROM0_BOOT_data), .in1(ROM1_TERMINAL_data), .out(multiplexer_22_out), .sel(COPY_MODE_q[3:1]));  // open: in2, in3, in4, in5, in6, in7
  not not_47 (not_47_out, and_22_out);
  not not_48 (not_48_out, IR_q_3[0]);
  not not_49 (not_49_out, IR_q_4[3]);
  not not_50 (not_50_out, IR_q_3[1]);
  and and_40 (and_40_out, not_14_out, not_49_out, IR_q_3[2], not_50_out, not_53_out);
  and and_41 (and_41_out, KERNEL_MODE_q, and_40_out);
  Register #(.width(1)) KERNEL_MODE (.D(or_33_out), .en(or_34_out), .clk(clock_1_out), .Q(KERNEL_MODE_q));  // open: clr
  Comparator #(.mode("unsigned"), .width(10)) comparator_9 (
    .a({PC_q_2, PC_q}), .b(10'hfb), .eq(comparator_9_eq));  // open: gt, lt
  not not_51 (not_51_out, comparator_10_eq);
  Register TST_LED (.D(demultiplexer_1_out3), .en(and_42_out), .clk(clock_1_out), .Q(TST_LED_q));  // open: clr
  and and_42 (and_42_out, not_47_out, decoder_5_out3);
  or or_30 (priority_encoder_2_p7, or_31_out, and_65_out);
  not not_52 (not_52_out, IR_q_3[1]);
  and and_43 (priority_encoder_1_p3, IR_q_4[3], IR_q_3[2], not_11_out, not_52_out, IR_q_3[0]);
  or or_31 (or_31_out, and_65_out, and_41_out, and_50_out);
  not not_53 (not_53_out, IR_q_3[0]);
  or or_32 (or_32_out, and_65_out, and_47_out);
  or or_33 (or_33_out, pla_1_out, comparator_8_eq, not_54_out);
  and and_44 (and_44_out, comparator_9_eq, INSTR_MODE_q);
  not not_54 (not_54_out, INSTR_MODE_q);
  Adder #(.width(10)) adder_9 (.a({PC_q_2, PC_q}), .b(multiplexer_26_out), .out(adder_9_out));  // open: cin, cout
  // LedBar #(.inputtype("row")) ledbar_1: pin names not known; wires that end beside it: TST_LED_q
  not not_55 (not_55_out, IR_q_3[0]);
  and and_45 (priority_encoder_2_p6, IR_q_4[3], IR_q_3[2], not_11_out, IR_q_3[1], not_55_out);
  not not_56 (not_56_out, IR_q_4[3]);
  not not_57 (not_57_out, IR_q_3[1]);
  and and_46 (and_46_out, not_14_out, not_56_out, IR_q_3[2], not_57_out, IR_q_3[0]);
  and and_47 (and_47_out, KERNEL_MODE_q, and_46_out);
  or or_34 (or_34_out, not_54_out, and_44_out, priority_encoder_3_p5);
  assign bit_extender_3_out = {{4{1'b0}}, COPY_MODE_q};  // Bit_Extender bit_extender_3
  and and_48 (and_48_out, IR_q_4[3], IR_q_3[2], not_11_out, IR_q_3[1], IR_q_3[0]);
  not not_58 (not_58_out, IR_q_4[3]);
  not not_59 (not_59_out, IR_q_3[0]);
  and and_49 (and_49_out, not_14_out, not_58_out, IR_q_3[2], IR_q_3[1], not_59_out);
  and and_50 (and_50_out, and_49_out, KERNEL_MODE_q);
  or or_35 (or_35_out, and_47_out, and_41_out);
  PLA #(.out_width(1), .\table ("00 0\n01 1\n10 0\n11 0")) pla_1 (.in(and_63_out), .out(pla_1_out));
  not not_60 (not_60_out, not_3_out);
  Register #(.width(24)) IR (
    .D(multiplexer_23_out), .en(and_38_out), .clk(clock_1_out),
    .Q({IR_q_4, IR_q_3, IR_q[18:16], IR_q_2, IR_q[12:8], IR_q_5}));  // open: clr
  Register #(.width(10)) PGRM_START_ADDR (
    .D({TWO_TMP_q, demultiplexer_1_out6}), .en(decoder_5_out6), .clk(clock_1_out), .Q(PGRM_START_ADDR_q));  // open: clr
  or or_36 (or_36_out, and_51_out, or_39_out, and_56_out);
  not not_61 (not_61_out, not_11_out);
  not not_62 (not_62_out, IR_q_3[2]);
  and and_51 (and_51_out, not_61_out, IR_q_4[3], not_62_out, IR_q_3[1], IR_q_3[0]);
  not not_63 (not_63_out, IR_q_4[3]);
  and and_52 (and_52_out, not_14_out, not_63_out, IR_q_3[2], IR_q_3[1], IR_q_3[0]);
  or or_37 (or_37_out, and_50_out, and_53_out);
  and and_53 (and_53_out, KERNEL_MODE_q, and_52_out);
  or or_38 (priority_encoder_3_p5, and_63_out[1], comparator_8_eq, and_63_out[0]);
  Multiplexer #(.width(24)) multiplexer_23 (
    .in0(multiplexer_24_out), .in1(24'h500000), .out(multiplexer_23_out), .sel(COPY_MODE_q[0]));
  Multiplexer #(.width(24)) multiplexer_24 (
    .in0(ROM0_BOOT_data), .in1(IRAM_dout), .out(multiplexer_24_out), .sel(INSTR_MODE_q));
  Comparator #(.mode("unsigned"), .width(24)) comparator_10 (
    .a(multiplexer_24_out), .b({24{1'b1}}), .eq(comparator_10_eq));  // open: gt, lt
  or or_39 (or_39_out, and_57_out, and_64_out, and_63_out[0]);
  or or_40 (or_40_out, and_65_out, and_62_out);
  or or_41 (or_41_out, and_50_out, and_41_out);
  or or_42 (or_42_out, and_65_out, or_41_out);
  or or_43 (or_43_out, and_13_out, or_42_out);
  and and_54 (and_54_out, or_51_out, or_43_out);
  Multiplexer #(.width(8)) multiplexer_25 (
    .in0({multiplexer_11_out_2[6], multiplexer_11_out}), .in1(multiplexer_7_out), .out(multiplexer_25_out),
    .sel(not_60_out));
  and and_55 (and_55_out, and_48_out, decoder_5_out4);
  Register #(.width(1)) INSTR_MODE (
    .D(bit_extender_4_out), .en(and_61_out), .clk(clock_1_out), .Q(INSTR_MODE_q));  // open: clr
  not not_64 (not_64_out, comparator_10_eq);
  not not_65 (not_65_out, IR_q_3[1]);
  not not_66 (not_66_out, IR_q_3[0]);
  and and_56 (and_56_out, not_61_out, IR_q_4[3], IR_q_3[2], not_65_out, not_66_out);
  not not_67 (not_67_out, IR_q_3[2]);
  not not_68 (not_68_out, IR_q_3[1]);
  not not_69 (not_69_out, IR_q_3[0]);
  and and_57 (and_57_out, not_14_out, IR_q_4[3], not_67_out, not_68_out, not_69_out);
  Register #(.width(10)) INT_RET_ADDR (
    .D(adder_6_out), .en(and_58_out), .clk(clock_1_out), .Q(INT_RET_ADDR_q));  // open: clr
  and and_58 (and_58_out, not_20_out, comparator_8_eq);
  or or_44 (and_63_out[1], and_26_out, and_59_out);
  and and_59 (and_59_out, and_64_out, not_73_out);
  D_Flip_Flop d_ff_5 (.D(comparator_10_eq), .clk(clock_1_out), .Q(d_ff_5_q));  // open: Qn, preset, reset
  or or_45 (or_45_out, and_47_out, and_53_out);
  or or_46 (or_46_out, and_62_out, or_45_out);
  and and_60 (and_60_out, or_46_out, or_51_out);
  RAM #(.addrWidth(10), .asyncread("true")) Main_RAM (
    .addr(multiplexer_29_out), .we(or_47_out), .oe(and_54_out), .clk(clock_1_out), .din(multiplexer_25_out),
    .dout(Main_RAM_dout));
  or or_47 (or_47_out, and_60_out, and_10_out);
  Register #(.width(1)) COPY_MODE (.D(or_48_out), .en(or_49_out), .clk(clock_1_out), .Q(COPY_MODE_q[0]));  // open: clr
  or or_48 (or_48_out, not_64_out, demultiplexer_1_out4[0]);
  or or_49 (or_49_out, comparator_10_eq, and_55_out);
  Register #(.width(3)) COPY_SRC (
    .D(demultiplexer_1_out4_2), .en(and_55_out), .clk(clock_1_out), .Q(COPY_MODE_q[3:1]));  // open: clr
  not not_70 (not_70_out, IR_q_3[1]);
  and and_61 (and_61_out, not_61_out, IR_q_4[3], IR_q_3[2], not_70_out, IR_q_3[0]);
  not not_71 (not_71_out, IR_q_3[2]);
  not not_72 (not_72_out, IR_q_3[1]);
  and and_62 (and_62_out, not_14_out, IR_q_4[3], not_71_out, not_72_out, IR_q_3[0]);
  not not_73 (not_73_out, d_ff_6_q);
  not not_74 (not_74_out, IR_q_3[0]);
  and and_63 (and_63_out[0], not_61_out, IR_q_4[3], IR_q_3[2], IR_q_3[1], not_74_out);
  D_Flip_Flop d_ff_6 (.D(d_ff_5_q), .clk(clock_1_out), .Q(d_ff_6_q));  // open: Qn, preset, reset
  Multiplexer #(.width(10)) multiplexer_26 (
    .in0({IR_q[9:8], IR_q_5}), .in1({TWO_TMP_q, multiplexer_8_out}), .out(multiplexer_26_out), .sel(IR_q[18]));
  Comparator #(.mode("unsigned"), .width(10)) comparator_11 (
    .a(multiplexer_29_out), .b(10'h3e0), .eq(comparator_11_eq), .lt(comparator_11_lt));  // open: gt
  and and_64 (and_64_out, not_61_out, IR_q_4[3], IR_q_3[2], IR_q_3[1], IR_q_3[0]);
  not not_75 (not_75_out, IR_q_3[2]);
  not not_76 (not_76_out, IR_q_3[0]);
  and and_65 (and_65_out, not_14_out, IR_q_4[3], not_75_out, IR_q_3[1], not_76_out);
  and and_66 (and_66_out, decoder_5_out2, and_48_out);
  or or_50 (or_50_out, and_66_out, priority_encoder_2_p8);
  or or_51 (or_51_out, comparator_11_eq, comparator_11_lt);
  Multiplexer #(.select(3), .width(10)) multiplexer_27 (
    .in0({PC_q_2, PC_q}), .in1(STACK_POINTER_q), .in2(CALL_STACK_POINTER_q), .in3(CALL_RET_ADDR_q),
    .in4(PGRM_START_ADDR_q), .in5(SYSRET_ADDR_q), .in6(INT_RET_ADDR_q),
    .out({multiplexer_27_out_2, multiplexer_27_out}), .sel(IR_q_2));  // open: in7
  Register #(.width(2)) TWO_TMP (
    .D(multiplexer_31_out), .en(or_50_out), .clk(clock_1_out), .Q(TWO_TMP_q));  // open: clr
  not not_77 (not_77_out, IR_q[18]);
  and and_67 (and_67_out, not_77_out, or_21_out);
  and and_68 (and_68_out, IR_q[18], or_21_out);
  or or_52 (or_52_out, or_32_out, and_67_out);
  or or_53 (or_53_out, and_68_out, or_37_out);
  // NOR_Gate nor_3 has open pins: in0=or_52_out, in1=priority_encoder_5_p4, in2=or_53_out, out=open
  // Priority_Encoder #(.select(2)) priority_encoder_5: pin names not known; wires that end beside it: priority_encoder_5_p1, priority_encoder_5_p2, or_53_out, priority_encoder_5_p4
  Register ERR_INFO (.D(demultiplexer_1_out5), .en(decoder_5_out5), .clk(clock_1_out), .Q(ERR_INFO_q));  // open: clr
  Multiplexer #(.select(2), .width(10)) multiplexer_28 (
    .in0({PC_q_2, PC_q}), .in1({IR_q[9:8], IR_q_5}), .in2({TWO_TMP_q, multiplexer_8_out}),
    .in3(multiplexer_16_out), .out(multiplexer_28_out), .sel(priority_encoder_5_p2));
  or or_54 (priority_encoder_5_p4, or_40_out, and_13_out, and_14_out);
  or or_55 (or_55_out, and_65_out, and_13_out);
  Multiplexer #(.width(10)) multiplexer_29 (
    .in0(multiplexer_28_out), .in1(subtractor_4_out), .out(multiplexer_29_out), .sel(or_55_out));
  Multiplexer #(.width(10)) multiplexer_30 (
    .in0({IR_q[9:8], IR_q_5}), .in1({TWO_TMP_q, multiplexer_8_out}), .out(multiplexer_30_out), .sel(IR_q[12]));
  or or_56 (priority_encoder_5_p1, or_52_out, or_35_out, and_57_out);
  PLA #(.in_width(10), .\table ("1111111111 11\n1111111110 10\n1111111101 01")) KBD_PLA (
    .in(multiplexer_29_out), .out(KBD_PLA_out));
  Comparator #(.mode("unsigned"), .width(10)) comparator_12 (
    .a(multiplexer_29_out), .b(10'h3fa), .eq(comparator_12_eq));  // open: gt, lt
  Comparator #(.mode("unsigned"), .width(10)) comparator_13 (
    .a(multiplexer_29_out), .b(10'h3f9), .eq(comparator_13_eq));  // open: gt, lt
  nor nor_4 (priority_encoder_3_p6, and_64_out, and_63_out[0], and_51_out, and_56_out);
  Demultiplexer #(.enable("true"), .select(3), .width(8)) demultiplexer_1 (
    .out0({demultiplexer_1_out0_2, demultiplexer_1_out0}),
    .out1({demultiplexer_1_out1_2, demultiplexer_1_out1}),
    .out2({demultiplexer_1_out2_2, demultiplexer_1_out2}), .out3(demultiplexer_1_out3),
    .out4({demultiplexer_1_out4_3, demultiplexer_1_out4_2, demultiplexer_1_out4[0]}),
    .out5(demultiplexer_1_out5), .out6(demultiplexer_1_out6),
    .in({multiplexer_11_out_2[6], multiplexer_11_out}), .sel(IR_q[18:16]), .en(and_48_out));  // open: out7
  Multiplexer #(.width(2)) multiplexer_31 (
    .in0(demultiplexer_1_out2), .in1(multiplexer_27_out_2), .out(multiplexer_31_out),
    .sel(priority_encoder_2_p8));
  Comparator #(.mode("unsigned"), .width(10)) comparator_14 (.a({IR_q[9:8], IR_q_5}), .b(10'h3e0));  // open: gt, eq, lt
  Multiplexer #(.width(3)) multiplexer_32 (
    .in0(IR_q_2), .in1({IR_q[17:16], IR_q_2[2]}), .out(multiplexer_32_out), .sel(or_21_out));
  Bit_Extender #(.in_width(10), .out_width(1), .\type ("zero")) bit_extender_4 (
    .in({IR_q[9:8], IR_q_5}), .out(bit_extender_4_out));
  Decoder #(.select(2)) decoder_3 (.out1(decoder_3_out1), .sel(KBD_PLA_out));  // open: out0, out2, out3, en
  and and_69 (and_69_out, and_63_out[0], not_39_out);
  Decoder #(.select(4)) decoder_4 (
    .out0(decoder_4_out0), .out1(decoder_4_out1), .out2(decoder_4_out2), .out3(decoder_4_out3),
    .out4(decoder_4_out4), .out5(decoder_4_out5), .out6(decoder_4_out6), .out7(decoder_4_out7),
    .out8(decoder_4_out8), .out9(decoder_4_out9), .out10(decoder_4_out10), .out11(decoder_4_out11),
    .out12(decoder_4_out12), .out13(decoder_4_out13), .out14(decoder_4_out14), .out15(decoder_4_out15),
    .sel({IR_q_2[0], IR_q[12:10]}), .en(or_21_out));
  Subtractor #(.width(10)) subtractor_4 (.a(multiplexer_28_out), .b(10'h1), .out(subtractor_4_out));  // open: bin, bout
  Multiplexer #(.width(8)) multiplexer_33 (
    .in0(multiplexer_34_out), .in1(bit_extender_7_out), .out(multiplexer_33_out), .sel(comparator_12_eq));
  Multiplexer #(.width(8)) multiplexer_34 (
    .in0(multiplexer_35_out), .in1(Main_RAM_dout), .out(multiplexer_34_out), .sel(or_51_out));
  Multiplexer #(.select(2), .width(8)) multiplexer_35 (
    .in1(bit_extender_5_out), .in2(bit_extender_6_out), .out(multiplexer_35_out));  // open: in0, in3, sel
  D_Flip_Flop d_ff_7 (.D(decoder_3_out1), .clk(clock_1_out), .Q(d_ff_7_q));  // open: Qn, preset, reset
  Register #(.width(24)) TOTAL_SYSCALLS (
    .D(adder_10_out), .en(and_69_out), .clk(clock_1_out),
    .Q({TOTAL_SYSCALLS_q_4, TOTAL_SYSCALLS_q_3, TOTAL_SYSCALLS_q_2, TOTAL_SYSCALLS_q}));  // open: clr
  Decoder #(.select(3)) decoder_5 (
    .out0(decoder_5_out0), .out1(decoder_5_out1), .out2(decoder_5_out2), .out3(decoder_5_out3),
    .out4(decoder_5_out4), .out5(decoder_5_out5), .out6(decoder_5_out6), .sel(IR_q[18:16]), .en(and_48_out));  // open: out7
  PLA #(.in_width(10), .\table ("1111111100 11\n1111111011 10")) TERM_PLA (.in(multiplexer_29_out), .out(TERM_PLA_out));
  and and_70 (and_70_out, KBD_PLA_out[0], KBD_PLA_out[1]);
  D_Flip_Flop d_ff_8 (.D(d_ff_7_q), .clk(clock_1_out), .Q(d_ff_8_q));  // open: Qn, preset, reset
  Adder #(.width(24)) adder_10 (
    .a({TOTAL_SYSCALLS_q_4, TOTAL_SYSCALLS_q_3, TOTAL_SYSCALLS_q_2, TOTAL_SYSCALLS_q}), .b(24'h1),
    .out(adder_10_out));  // open: cin, cout
  Decoder #(.select(2)) decoder_6 (
    .out2(decoder_6_out2), .out3(decoder_6_out3), .sel(TERM_PLA_out));  // open: out0, out1, en
  xor xor_6 (xor_6_out, FLAGS_q[2], FLAGS_q[3]);
  xor xor_7 (xor_7_out, FLAGS_q[2], FLAGS_q[3]);
  xor xor_8 (xor_8_out, FLAGS_q[2], FLAGS_q[3]);
  xor xor_9 (xor_9_out, FLAGS_q[2], FLAGS_q[3]);
  Hex_Digit_Display hex_digit_display_1 (.value(TOTAL_CYCLES_q[31:28]));  // open: dp
  Hex_Digit_Display hex_digit_display_2 (.value(TOTAL_CYCLES_q[27:24]));  // open: dp
  TTY #(.cols(109), .rows(32)) tty_1 (
    .data(multiplexer_11_out), .clk(not_39_out), .we(decoder_6_out3), .clr(and_71_out));
  and and_71 (and_71_out, not_78_out, decoder_6_out2);
  not not_78 (not_78_out, decoder_6_out3);
  and and_72 (and_72_out, and_70_out, multiplexer_11_out[0]);
  not not_79 (not_79_out, FLAGS_q[1]);
  not not_80 (not_80_out, FLAGS_q[0]);
  not not_81 (not_81_out, xor_6_out);
  not not_82 (not_82_out, FLAGS_q[1]);
  not not_83 (not_83_out, FLAGS_q[1]);
  not not_84 (not_84_out, xor_8_out);
  Hex_Digit_Display hex_digit_display_3 (.value(TOTAL_CYCLES_q[23:20]));  // open: dp
  Hex_Digit_Display hex_digit_display_4 (.value(TOTAL_CYCLES_q[19:16]));  // open: dp
  and and_73 (and_73_out, decoder_4_out0, FLAGS_q[2]);
  and and_74 (and_74_out, decoder_4_out1, not_85_out);
  not not_85 (not_85_out, FLAGS_q[2]);
  and and_75 (and_75_out, decoder_4_out2, FLAGS_q[1]);
  and and_76 (and_76_out, decoder_4_out3, not_86_out);
  not not_86 (not_86_out, FLAGS_q[1]);
  and and_77 (and_77_out, decoder_4_out4, FLAGS_q[0]);
  and and_78 (and_78_out, decoder_4_out5, not_87_out);
  not not_87 (not_87_out, FLAGS_q[0]);
  and and_79 (and_79_out, decoder_4_out6, FLAGS_q[3]);
  and and_80 (and_80_out, decoder_4_out7, not_88_out);
  not not_88 (not_88_out, FLAGS_q[3]);
  and and_81 (and_81_out, decoder_4_out8, and_82_out);
  and and_82 (and_82_out, FLAGS_q[0], not_79_out);
  and and_83 (and_83_out, decoder_4_out9, or_57_out);
  or or_57 (or_57_out, not_80_out, FLAGS_q[1]);
  and and_84 (and_84_out, decoder_4_out10, or_58_out);
  or or_58 (or_58_out, FLAGS_q[1], not_81_out);
  and and_85 (and_85_out, decoder_4_out11, and_86_out);
  and and_86 (and_86_out, not_82_out, xor_7_out);
  and and_87 (and_87_out, decoder_4_out12, and_88_out);
  and and_88 (and_88_out, not_83_out, not_84_out);
  and and_89 (and_89_out, decoder_4_out13, or_59_out);
  or or_59 (or_59_out, FLAGS_q[1], xor_9_out);
  and and_90 (and_90_out, decoder_4_out14, 1'b1);
  buf and_91 (and_91_out, decoder_4_out15);  // AND_Gate
  Hex_Digit_Display hex_digit_display_5 (.value(TOTAL_CYCLES_q[15:12]));  // open: dp
  Hex_Digit_Display hex_digit_display_6 (.value(TOTAL_CYCLES_q[11:8]));  // open: dp
  Keyboard keyboard_1 (.clk(d_ff_8_q), .re(1'b1), .avail(keyboard_1_avail), .data(keyboard_1_data));  // open: clr
  Hex_Digit_Display hex_digit_display_7 (.value(TOTAL_CYCLES_q[7:4]));  // open: dp
  Hex_Digit_Display hex_digit_display_8 (.value(TOTAL_CYCLES_q[3:0]));  // open: dp
  Hex_Digit_Display hex_digit_display_9 (.value(TOTAL_SYSCALLS_q_4));  // open: dp
  or or_60 (priority_encoder_3_p2, and_73_out, and_74_out, and_75_out, and_76_out, and_77_out, and_78_out, and_79_out, and_80_out, and_81_out, and_83_out, and_84_out, and_85_out, and_87_out, and_89_out, and_90_out, and_91_out);
  Hex_Digit_Display hex_digit_display_10 (.value(TOTAL_SYSCALLS_q_3));  // open: dp
  Hex_Digit_Display hex_digit_display_11 (.value(TOTAL_SYSCALLS_q_2));  // open: dp
  assign bit_extender_5_out = {{1{1'b0}}, keyboard_1_data};  // Bit_Extender bit_extender_5
  assign bit_extender_6_out = {{7{1'b0}}, keyboard_1_avail};  // Bit_Extender bit_extender_6
  Hex_Digit_Display hex_digit_display_12 (.value(TOTAL_SYSCALLS_q[11:8]));  // open: dp
  Hex_Digit_Display hex_digit_display_13 (.value(TOTAL_SYSCALLS_q[7:4]));  // open: dp
  or or_61 (or_61_out, in_2, comparator_13_eq);
  Hex_Digit_Display hex_digit_display_14 (.value(TOTAL_SYSCALLS_q[3:0]));  // open: dp
  Register #(.width(1)) ENTER (.D(xor_10_out), .en(or_61_out), .clk(clock_1_out), .Q(ENTER_q));  // open: clr
  xor xor_10 (xor_10_out, comparator_13_eq, in_2);
  Hex_Digit_Display hex_digit_display_15 (.value(register_1_q_6));  // open: dp
  Hex_Digit_Display hex_digit_display_16 (.value(register_1_q_5));  // open: dp
  assign bit_extender_7_out = {{7{1'b0}}, ENTER_q};  // Bit_Extender bit_extender_7
  Hex_Digit_Display hex_digit_display_17 (.value(register_1_q_4));  // open: dp
  Hex_Digit_Display hex_digit_display_18 (.value(register_1_q_3));  // open: dp
  Hex_Digit_Display hex_digit_display_19 (.value(register_1_q_2));  // open: dp
  Hex_Digit_Display hex_digit_display_20 (.value(register_1_q));  // open: dp
  Hex_Digit_Display hex_digit_display_21 (.value(ERR_INFO_q[7:4]));  // open: dp
  Hex_Digit_Display hex_digit_display_22 (.value(ERR_INFO_q[3:0]));  // open: dp

  // Notes on the sheet:
  //   N
  //   Z
  //   C
  //   V
  //   V flag
  //   C flag
  //   N flag
  //   Z flag
  //   ALU_OUT
  //   READ A
  //   WE gate
  //   testing if inst needs alu or not
  //   READ_A
  //   READ B
  //   CMP needs to subtract and not write result, override normal selection
  //   READ_B
  //   DATA BUS
  //   MOV: 01000
  //   HALT: 10000
  //   main register part of address bus
  //   main register select for address bus
  //   contents of ROM1_TERMINAL (hex, n*v repeats v):
  //   275*0 480000 490001 c82000 c80000 480003 f00000 e00000 d40000 480002 490001 c82000 c80000 480003
  //   f00000 c88000 480002 f00000 48000a c80000 480001 f00000 e00000 4c0000 4d0001 4f0050 4e0070 c8a000
  //   c8e000 c88000 480006 f00000 9fc000 880936 7a000 88392d 4f0050 e00000 4f0050 c82000 c8e000 480008
  //   f00000 4a0000 984000 e00000 7d2000 c82000 d8011a e00000 420000 c88000 c84000 480007 f00000 430000
  //   2e000 c88000 c84000 480007 f00000 420000 c86000 c84000 48000a f00000 e00000 480005 f00000 d80113
  //   e00000 480009 f00000 4f0002 4e0000 4d0001 4c0008 c8e000 c8c000 480007 f00000 c80000 480002 f00000
  //   4b0020 c86000 480001 f00000 6a000 9cc000 880d5f 48000a c80000 480001 f00000 d80113 e00000 4f0000
  //   4e0001 4c0001 c8c000 c8e000 480007 f00000 420000 c84000 480002 f00000 4d001f 25e000 48001f 9d0000
  //   880d88 49000a c82000 480001 f00000 88398c 490020 c82000 480001 f00000 78000 88118f 883976 4d0002
  //   9ea000 880d98 48000a c80000 480001 f00000 d80159 e00000 68000 883976 480002 f00000 48000a c80000
  //   480001 f00000 d80113 e00000 4b0002 c86000 4b00af c86000 480007 f00000 440000 4f0001 4b00a0 490002
  //   c82000 c86000 480007 f00000 d80144 c80000 d80113 e00000 4b0002 c86000 4b00af c86000 480007 f00000
  //   c80000 4b00a0 490002 c82000 c86000 480007 f00000 c80000 480003 f00000 48000a c80000 480001 f00000
  //   d80113 e00000 c80000 480002 f00000 480020 c80000 480001 f00000 e00000 700000 d801ca 702000 d801ca
  //   704000 d801ca 706000 d801ca 708000 d801ca 70a000 d801ca 48000a c80000 480001 f00000 d80113 e00000
  //   714000 c82000 480002 f00000 c86000 480002 f00000 480020 c80000 480001 f00000 e00000 5b0000 d801e4
  //   5b2000 d801e4 5b4000 d801e4 5b6000 d801e4 5b8000 d801e4 5ba000 d801e4 5bc000 d801e4 48000a c80000
  //   480001 f00000 d80113 e00000 4b0002 c86000 4b00af c86000 480007 f00000 440000 4f0001 4b00a0 490002
  //   c82000 c86000 480007 f00000 d80144 450000 4b00a1 490002 c82000 c86000 480007 f00000 d80144 460000
  //   4b00a2 490002 c82000 c86000 480007 f00000 d80144 470000 c8a000 c8c000 c8e000 480006 f00000 d80113
  //   e00000 4b0002 c86000 4b00af c86000 480007 f00000 440000 4f0001 4b00a0 490002 c82000 c86000 480007
  //   f00000 d80144 450000 4b00a1 490002 c82000 c86000 480007 f00000 d80144 460000 c8a000 c8c000 480007
  //   f00000 c80000 480002 f00000 48000a c80000 480001 f00000 d80113 e00000 490001 c82000 490000 c82000
  //   49003e c82000 480006 f00000 490001 c82000 490001 c82000 490000 c82000 480006 f00000 490001 c82000
  //   490002 c82000 490045 c82000 480006 f00000 490001 c82000 490003 c82000 49003a c82000 480006 f00000
  //   490001 c82000 490004 c82000 490000 c82000 480006 f00000 490001 c82000 490005 c82000 490063 c82000
  //   480006 f00000 490001 c82000 490006 c82000 490000 c82000 480006 f00000 490001 c82000 490007 c82000
  //   490072 c82000 480006 f00000 490001 c82000 490008 c82000 490000 c82000 480006 f00000 490001 c82000
  //   490009 c82000 490070 c82000 480006 f00000 490001 c82000 49000a c82000 49006d c82000 480006 f00000
  //   490001 c82000 49000b c82000 490000 c82000 480006 f00000 490001 c82000 49000c c82000 490070 c82000
  //   480006 f00000 490001 c82000 49000d c82000 490073 c82000 480006 f00000 490001 c82000 49000e c82000
  //   490068 c82000 480006 f00000 490001 c82000 49000f c82000 490000 c82000 480006 f00000 490001 c82000
  //   490010 c82000 490070 c82000 480006 f00000 490001 c82000 490011 c82000 49006f c82000 480006 f00000
  //   490001 c82000 490012 c82000 490070 c82000 480006 f00000 490001 c82000 490013 c82000 490000 c82000
  //   480006 f00000 490001 c82000 490014 c82000 490073 c82000 480006 f00000 490001 c82000 490015 c82000
  //   490000 c82000 480006 f00000 490001 c82000 490016 c82000 49006c c82000 480006 f00000 490001 c82000
  //   490017 c82000 490000 c82000 480006 f00000 490001 c82000 490018 c82000 490072 c82000 480006 f00000
  //   490001 c82000 490019 c82000 490073 c82000 480006 f00000 490001 c82000 49001a c82000 490000 c82000
  //   480006 f00000 490001 c82000 49001b c82000 490072 c82000 480006 f00000 490001 c82000 49001c c82000
  //   490061 c82000 480006 f00000 490001 c82000 49001d c82000 490000 c82000 480006 f00000 490001 c82000
  //   49001e c82000 490065 c82000 480006 f00000 490001 c82000 49001f c82000 490063 c82000 48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
  //   00111 INTRET
  //   k_upper
  //   k_lower
  //   LDI: 01001
  //   JOC: 10001
  //   NOP: 01010
  //   JROC: 10010
  //   syscall handler addr
  //   int_handler
  //   SP_INITIAL
  //   RAR: 01011
  //   kpanic_addr
  //   NOTE: 5th bit is middle gate here
  //   ADC: 01100
  //   for WE gate
  //   CMP: 10011
  //   early boot end
  //   contents of ROM0_BOOT (hex, n*v repeats v):
  //   e80000 c003c0 480042 a803fc 480001 7c0000 490000 7a2000 49000b 982000 881102 490041 2000 b10000
  //   d83000 f80000 e80001 48004f a803fc d80050 d80067 48004f a803fc 480046 a80060 48004c a80061 480041
  //   a80062 480047 a80063 48007b a80064 480033 a80065 480065 a80066 480063 a80067 480038 a80068 48007d
  //   a80069 480030 a80210 480031 a80211 480032 a80212 480033 a80213 480034 a80214 480035 a80215 480036
  //   a80216 480037 a80217 480038 a80218 480039 a80219 480061 a8021a 480062 a8021b 480063 a8021c 480064
  //   a8021d 480065 a8021e 480066 a8021f 480054 a803fc 480001 c80000 883906 48006a a80041 48006c a80042
  //   48006f a80043 4800a3 a80044 4800c5 a80045 4800c6 a80046 4800c9 a80047 4800da a80048 4800af a80049
  //   4800f8 a8004a 480092 a8004b e00000 480050 a80051 e00000 a003fd e00000 d00000 a803fc e00000 d00000
  //   410000 4a000f 204000 4a00f0 214000 4a0004 794000 190000 4a0002 7a4000 4a0010 4000 b00000 14000
  //   b12000 420000 c82000 d8006c c84000 d8006c 4a0001 794000 e00000 490000 4a0010 22000 b34000 986000
  //   880890 4b0001 16000 883888 c82000 e00000 480002 7a0000 d00000 a80200 d00000 d80087 a00200 d80087
  //   480004 790000 d10000 d00000 100000 2000 490001 792000 e00000 d00000 d10000 7a2000 b10000 4a0000
  //   994000 8808ae a823fc 4a0001 4000 8838a6 e00000 d00000 d10000 4a0001 7a4000 b20000 b32000 9a6000
  //   880cc1 4c0000 9a8000 880cbd 9b8000 8808c3 8838bd 4a0001 4000 14000 8838b3 480001 e00000 480000
  //   e00000 e00000 480001 a803fb e00000 d00000 d10000 d20000 a82201 490001 9a2000 8808d6 490002 9a2000
  //   8808d6 4900a1 d800ef e00000 a10201 7a4000 b82000 e00000 d10000 d00000 a82201 490001 982000 8808e6
  //   490002 982000 8808e6 4900a0 d800ef e00000 a10201 7a0000 b02000 e00000 49004b a823fc 49003a a823fc
  //   e00000 7d2000 a821ff d800ea a101ff c82000 d8006f 49000a a823fc e00000 d00000 a80200 a82201 a84202
  //   a86203 a88204 a8a205 a8c206 a8e207 e00000 4900ee 7d2000 d800ef d80000 d00000 490050 10000 4a0000
  //   7a4000 b22000 490002 7a2000 7e4000 100000 490001 2000 7c0000 ffffff 883810
  //   SBC: 01101
  //   LD: 10100
  //   JROC logic
  //   RSR: 01110
  //   ST: 10101
  //   WSR: 01111
  //   LDR: 10110
  //   CALL:  11011
  //   STR: 10111
  //   RET:  11100
  //   ISP: 11000
  //   CIM:  11101
  //   PUSH: 11001
  //   SYSCALL: 11110
  //   ADDRESS BUS
  //   SYSRET:  11111
  //   POP: 11010
  //   CTRL BUS
  //   DATA BUS
  //   IMM10 mode: Direct 10 bits from IW
  //   program counter value
  //   register value + 2 temp bits
  //   stack pointer
  //   instructions which disable the interrupt
  //   WSR_FLAGS
  //   WSR_SHIFT_AMOUNT
  //   COND_CODE
  //   RS for JOC
  //   WSR logic
  //   DATA BUS
  //   CLK_CYCLES
  //   0000 NEG
  //   0001 POS
  //   0011 NZE
  //   0100 UGE
  //   0101 ULT
  //   0110 OV
  //   1001 ULE
  //   1010 SGE
  //   1011 SLT
  //   1100 SGT
  //   1101 SLE
  //   1110 UN
  //   0010 ZE/EQ
  //   0111 NOV
  //   1000 UGT
  //   1111 reserved
  //   SYSTEM_CALLS
  //   FUNCTION_CALLS
  //   LAST_ERR_CODE
endmodule
